# Fritzing sketch clock-module (saved by Fritzing 1.0.4)
breadboards: 1

parts:
  R2 = Resistor [tolerance=±5% resistance=1k package="1206 [SMD]"]
  R3 = Resistor [tolerance=±5% resistance=220 package="1206 [SMD]"]
  C4 = Ceramic Capacitor [capacitance=10nF voltage=35V package="200 mil [THT, multilayer]"]
  C5 = Ceramic Capacitor [capacitance=100nF voltage=35V package="200 mil [THT, multilayer]"]
  R4 = Resistor [tolerance=±5% resistance=1k package="1206 [SMD]"]
  R5 = Resistor [tolerance=±5% resistance=1k package="1206 [SMD]"]
  R6 = Resistor [tolerance=±5% resistance=220 package="1206 [SMD]"]
  C6 = Ceramic Capacitor [capacitance=10nF voltage=35V package="200 mil [THT, multilayer]"]
  C7 = Ceramic Capacitor [capacitance=100nF voltage=35V package="200 mil [THT, multilayer]"]
  R7 = Resistor [tolerance=±5% resistance=1M package="1206 [SMD]"]
  LED4 = smd LED [color="Blue (430nm)" package="0805 [SMD]"]
  R8 = Resistor [tolerance=±5% resistance=220 package="1206 [SMD]"]
  R9 = Resistor [tolerance=±5% resistance=1k package="1206 [SMD]"]
  R10 = Resistor [tolerance=±5% resistance=1k package="1206 [SMD]"]
  C9 = Ceramic Capacitor [capacitance=10nF voltage=35V package="200 mil [THT, multilayer]"]
  74LS1 = 74LS00 [package="DIP (Dual Inline) [THT]"]
  74LS2 = 74LS00 [package="DIP (Dual Inline) [THT]"]
  LED5 = smd LED [color="Blue (430nm)" package="0805 [SMD]"]
  LED7 = smd LED [color="Red (633nm)" package="0805 [SMD]"]
  R11 = Resistor [tolerance=±5% resistance=220 package="1206 [SMD]"]  # not connected
  R13 = Rotary Potentiometer (Small) [maximum_resistance=1MΩ knob_status=50% power=0.5W package=THT]
  C3 = Electrolytic Capacitor [capacitance=1μF voltage=50V package="100 mil [THT, electrolytic]"]
  U3 = 555 Timer [package="DIP8 [THT]"]  # not connected
  U2 = 555 Timer [package="DIP8 [THT]"]  # not connected
  LED6 = smd LED [color="Blue (430nm)" current=0A package="0805 [SMD]"]
  S3 = Toggle Switch [package=THT]
  S1 = Pushbutton [package="[THT]"]
  U1 = 555 Timer [package="SO8 [SMD]"]  # not connected
  Part1 = Arduino Uno (Rev3)

nets:
  N1: R2.Pin_0, R13.leg1
  N2: R2.Pin_1, R4.Pin_1
  N3: R3.Pin_0, LED6.cathode
  GND: R3.Pin_1, C4.0, C5.0, R6.Pin_1, C6.0, C7.0, R8.Pin_1, C9.0, 74LS1.GND, 74LS2.1A, 74LS2.1B, 74LS2.2Y, 74LS2.GND, LED7.cathode, C3.-, S3.COM, S1.Pin_3, S1.Pin_4, Part1.GND
  VCC: C5.1, R4.Pin_0, R5.Pin_1, R7.Pin_0, R9.Pin_1, R10.Pin_1, 74LS1.Vcc, 74LS2.2A, 74LS2.2B, 74LS2.Vcc
  N4: R5.Pin_0, S1.Pin_1, S1.Pin_2
  N5: R6.Pin_0, LED5.cathode
  N6: C7.1, R7.Pin_1
  N7: LED4.cathode, R8.Pin_0
  N8: LED4.anode, 74LS1.1B, 74LS1.2A, 74LS1.2B
  N9: R9.Pin_0, S3.L2
  N10: R10.Pin_0, S3.L1
  N11: 74LS1.1A, LED6.anode
  N12: 74LS1.1Y, 74LS1.3A
  N13: 74LS1.2Y, 74LS1.4B
  N14: 74LS1.3Y, 74LS2.4B
  N15: 74LS1.3B, 74LS1.4Y
  N16: 74LS1.4A, LED5.anode
  N17: 74LS2.1Y, 74LS2.4A
  N18: 74LS2.3Y, Part1.A0
  N19: 74LS2.3A, 74LS2.3B, 74LS2.4Y
  N20: R13.wiper, C3.+

custom parts:
  74LS00: Quad 2-Input NAND Gate
