# Fritzing sketch toggle-switch (saved by Fritzing 1.0.4)
breadboards: 1

parts:
  LED1 = LED - 5mm [color="Red (633nm)" current=0.030A package="5 mm [THT]"]
  R1 = Resistor [tolerance=±5% power=0.25W resistance=220 package=THT]
  R2 = Resistor [tolerance=±5% power=0.25W resistance=220 package=THT]
  LED2 = LED - 5mm [color="Green (555nm)" current=0.030A package="5 mm [THT]"]
  S1 = Toggle Switch [package=THT]
  Part1 = Arduino Uno (Rev3)

nets:
  N1: LED1.cathode, LED2.cathode, S1.COM, Part1.GND
  N2: LED1.anode, R1.Pin_0, S1.L1, Part1.A0
  N3: R1.Pin_1, R2.Pin_1
  N4: R2.Pin_0, LED2.anode, S1.L2, Part1.A1
